// Logisim project Lab2Problem2.circ as structural Verilog: 1 circuit, main circuit main
module main (
  input  switch_car_6,
  input  switch_car_5,
  input  switch_car_4,
  input  switch_car_3,
  input  switch_car_2,
  input  switch_car_1,
  input  switch_car_0
);

  wire _0_1_2_3_4_out, _0_1_3_4_5_6_out, _0_2_3_5_6_2_out, _0_2_3_5_6_out, _0_2_6_out, _0_4_5_6_out,
       _0000001_2_out, _0000001_out, _2_3_4_5_6_out, _0000010_2_out, _0000010_out, _0000100_2_out,
       _0000100_out, _0001000_2_out, _0001000_out, _0010000_2_out, _0010000_out, _0100000_2_out,
       _0100000_out, _1000000_2_out, _1000000_out, bus_0_out, bus_1_out, bus_2_out, not_1_out, not_2_out,
       not_3_out, not_4_out, not_5_out, not_6_out, not_7_out, not_8_out, not_9_out, not_10_out;

  not not_1 (not_1_out, switch_car_6);
  not not_2 (not_2_out, switch_car_5);
  not not_3 (not_3_out, switch_car_4);
  not not_4 (not_4_out, switch_car_3);
  not not_5 (not_5_out, switch_car_2);
  not not_6 (not_6_out, switch_car_1);
  not not_7 (not_7_out, switch_car_0);
  and _0000001 (_0000001_out, switch_car_0, not_6_out, not_5_out, not_4_out, not_3_out, not_2_out, not_1_out);
  and _0000010 (_0000010_out, not_7_out, switch_car_1, not_5_out, not_4_out, not_3_out, not_2_out, not_1_out);
  or bus_0 (bus_0_out, _0000001_out, _0000100_out, _0010000_out, _1000000_2_out);
  and _0000100 (_0000100_out, not_7_out, not_6_out, switch_car_2, not_4_out, not_3_out, not_2_out, not_1_out);
  or bus_1 (bus_1_out, _0000010_out, _0000100_out, _0100000_out, _1000000_2_out);
  not not_8 (not_8_out, bus_0_out);
  and _0001000 (_0001000_out, not_7_out, not_6_out, not_5_out, switch_car_3, not_3_out, not_2_out, not_1_out);
  or bus_2 (bus_2_out, _0001000_out, _0010000_out, _0100000_out, _1000000_2_out);
  not not_9 (not_9_out, bus_1_out);
  and _0010000 (_0010000_out, not_7_out, not_6_out, not_5_out, not_4_out, switch_car_4, not_2_out, not_1_out);
  not not_10 (not_10_out, bus_2_out);
  and _0100000 (_0100000_out, not_7_out, not_6_out, not_5_out, not_4_out, not_3_out, switch_car_5, not_1_out);
  and _1000000 (_1000000_out, bus_2_out, bus_1_out, bus_0_out);
  and _0100000_2 (_0100000_2_out, bus_2_out, bus_1_out, not_8_out);
  and _0010000_2 (_0010000_2_out, bus_2_out, not_9_out, bus_0_out);
  and _0001000_2 (_0001000_2_out, bus_2_out, not_9_out, not_8_out);
  and _0000100_2 (_0000100_2_out, not_10_out, bus_1_out, bus_0_out);
  and _0000010_2 (_0000010_2_out, not_10_out, bus_1_out, not_8_out);
  and _0000001_2 (_0000001_2_out, not_10_out, not_9_out, bus_0_out);
  and _1000000_2 (_1000000_2_out, not_7_out, not_6_out, not_5_out, not_4_out, not_3_out, not_2_out, switch_car_6);
  or _2_3_4_5_6 (_2_3_4_5_6_out, _0000100_2_out, _0001000_2_out, _0010000_2_out, _0100000_2_out, _1000000_out);
  or _0_4_5_6 (_0_4_5_6_out, _0000001_2_out, _0010000_2_out, _0100000_2_out, _1000000_out);
  or _0_2_3_5_6 (_0_2_3_5_6_out, _0000001_2_out, _0000100_2_out, _0001000_2_out, _0100000_2_out, _1000000_out);
  or _0_1_2_3_4 (_0_1_2_3_4_out, _0000001_2_out, _0000010_2_out, _0000100_2_out, _0001000_2_out, _0010000_2_out);
  or _0_2_6 (_0_2_6_out, _0000001_2_out, _0000100_2_out, _1000000_out);
  or _0_2_3_5_6_2 (_0_2_3_5_6_2_out, _0000001_2_out, _0000100_2_out, _0001000_2_out, _0100000_2_out, _1000000_out);
  or _0_1_3_4_5_6 (_0_1_3_4_5_6_out, _0000001_2_out, _0000010_2_out, _0001000_2_out, _0010000_2_out, _0100000_2_out, _1000000_out);
  _7_Segment_Display u_7_segment_display_1 (
    .g(_2_3_4_5_6_out), .f(_0_4_5_6_out), .a(_0_2_3_5_6_out), .b(_0_1_2_3_4_out), .e(_0_2_6_out),
    .d(_0_2_3_5_6_2_out), .c(_0_1_3_4_5_6_out));  // open: dp
endmodule
