// Logisim project Lab3Prob2.circ as structural Verilog: 1 circuit, main circuit main
module main (
);

  wire and_1_out, and_2_out, and_3_out, and_4_out, and_5_out, and_7_out, and_8_out, and_9_out, and_10_out,
       and_11_out, and_12_out, and_13_out, Button_out, Clock_out, nor_1_out, nor_2_out, nor_3_out, nor_4_out,
       nor_6_out, nor_7_out, nor_8_out, nor_9_out, not_1_out, not_3_out, not_4_out, not_5_out, not_6_out,
       not_7_out, not_8_out, not_9_out, not_10_out, or_1_out, or_3_out, Reset_out, xor_2_out;

  Button Reset (.out(Reset_out));
  Clock Clock (.out(Clock_out));
  not not_1 (not_1_out, Button_out);
  Button Button (.out(Button_out));
  nor nor_1 (nor_1_out, and_1_out, nor_3_out);
  and and_1 (and_1_out, nor_4_out, Clock_out);
  nor nor_2 (nor_2_out, and_2_out, nor_4_out);
  and and_2 (and_2_out, or_3_out, not_6_out);
  // NOT_Gate not_2 is placed but not wired
  not not_3 (not_3_out, nor_3_out);
  nor nor_3 (nor_3_out, nor_1_out, and_3_out);
  and and_3 (and_3_out, Clock_out, not_4_out);
  not not_4 (not_4_out, nor_4_out);
  nor nor_4 (nor_4_out, nor_2_out, or_1_out);
  or or_1 (or_1_out, and_4_out, and_5_out);
  and and_4 (and_4_out, Reset_out, not_6_out);
  and and_5 (and_5_out, not_6_out, not_5_out);
  not not_5 (not_5_out, or_3_out);
  not not_6 (not_6_out, Clock_out);
  // AND_Gate and_6 is placed but not wired
  // NOR_Gate nor_5 is placed but not wired
  not not_7 (not_7_out, nor_8_out);
  nor nor_6 (nor_6_out, and_7_out, nor_8_out);
  and and_7 (and_7_out, nor_9_out, Clock_out);
  nor nor_7 (nor_7_out, and_8_out, nor_9_out);
  and and_8 (and_8_out, Button_out, not_8_out);
  not not_8 (not_8_out, Clock_out);
  // OR_Gate or_2 is placed but not wired
  // XOR_Gate xor_1 is placed but not wired
  nor nor_8 (nor_8_out, nor_6_out, and_9_out);
  and and_9 (and_9_out, Clock_out, not_9_out);
  not not_9 (not_9_out, nor_9_out);
  nor nor_9 (nor_9_out, nor_7_out, and_10_out);
  and and_10 (and_10_out, not_8_out, not_10_out);
  not not_10 (not_10_out, Button_out);
  xor xor_2 (xor_2_out, nor_3_out, nor_8_out);
  and and_11 (and_11_out, not_3_out, nor_8_out, not_1_out);
  and and_12 (and_12_out, nor_3_out, not_7_out);
  and and_13 (and_13_out, nor_3_out, nor_8_out, Button_out);
  LED led_1 (.in(xor_2_out));
  or or_3 (or_3_out, and_11_out, and_12_out, and_13_out);

  // Notes on the sheet:
  //   74XX Gates
  //   and their pins
  //   7404
  //   1             2
  //   7408
  //   1
  //   2
  //   S1
  //   D1
  //   7402
  //   3
  //   3
  //   2
  //   7486
  //   3
  //   1
  //   2
  //   7432
  //   1
  //   3
  //   1
  //   2
  //   S0
  //   D0
  //   D0
  //   D1
endmodule
