// Logisim project Lab3Prob3.circ as structural Verilog: 1 circuit, main circuit main
module main (
  input  in_1,
  input  in_2,
  input  in_3,
  input  in_4,
  input  in_5,
  input  I_O_Enable,
  input  Enable,
  output out_8,
  output out_9,
  output out_10,
  output out_11
);

  wire and_1_out, and_2_out, and_3_out, and_4_out, and_5_out, and_6_out, and_7_out, and_8_out, and_9_out,
       and_10_out, and_11_out, and_12_out, and_13_out, and_14_out, and_15_out, Clear_out, clock_1_out,
       clock_2_out, D0_out, D1_out, D2_out, D3_out, Engine_out, multiplexer_1_out, not_1_out, not_2_out,
       not_3_out, not_4_out, not_5_out, not_6_out, not_7_out, not_8_out, not_9_out, not_10_out, not_11_out,
       not_12_out, not_13_out, not_14_out, not_16_out, not_17_out, not_18_out, not_19_out, not_20_out,
       not_21_out, or_1_out, Reset_2_out, Reset_out, s1xs0_out, Wipers_out, xor_1_out, xor_2_out;
  wire [1:0] not_15_out, register_2_q, register_5_q;
  wire [1:1] or_3_out;
  wire [3:0] register_1_q, register_3_q;

  Button Clear (.out(Clear_out));
  not not_1 (not_1_out, 1'b0);
  not not_2 (not_2_out, 1'b0);
  xor s1xs0 (s1xs0_out, 1'b0, 1'b0);
  Register #(.width(4)) register_1 (.D(4'b0000), .en(Enable), .Q(register_1_q), .clk(clock_1_out), .clr(Clear_out));
  Clock clock_1 (.out(clock_1_out));
  and and_1 (and_1_out, not_1_out, not_2_out);
  or or_1 (or_1_out, and_1_out, s1xs0_out);
  buf _0 (register_1_q[0], not_3_out);  // AND_Gate
  not not_3 (not_3_out, 1'b0);
  not not_4 (not_4_out, 1'b0);
  and and_2 (and_2_out, not_4_out, 1'b0, 1'b0, 1'b0);
  and and_3 (and_3_out, 1'b0, not_5_out);
  not not_5 (not_5_out, 1'b0);
  and and_4 (and_4_out, 1'b0, 1'b0, not_6_out, not_7_out);
  not not_6 (not_6_out, 1'b0);
  not not_7 (not_7_out, 1'b0);
  and and_5 (and_5_out, 1'b0, 1'b0, s1xs0_out);
  not not_8 (not_8_out, 1'b0);
  not not_9 (not_9_out, 1'b0);
  and and_6 (and_6_out, not_8_out, not_9_out, 1'b0, 1'b0);
  not not_10 (not_10_out, 1'b0);
  and and_7 (and_7_out, not_10_out, 1'b0, or_1_out);
  and and_8 (and_8_out, or_1_out, 1'b0, 1'b0);
  not not_11 (not_11_out, 1'b0);
  and and_9 (and_9_out, 1'b0, not_11_out, 1'b0, 1'b0);
  buf _1 (register_1_q[1], s1xs0_out);  // AND_Gate
  or _3 (register_1_q[3], and_2_out, and_3_out, and_4_out, and_5_out);
  or _2 (register_1_q[2], and_6_out, and_7_out, and_8_out, and_9_out);
  Register #(.width(2)) register_2 (.D(not_15_out), .Q(register_2_q), .clk(clock_1_out), .clr(Reset_out));  // open: en
  Register #(.width(4)) register_3 (
    .D({in_4, in_3, in_2, in_1}), .Q(register_3_q), .clk(clock_1_out));  // open: en, clr
  Button Reset (.out(Reset_out));
  xor xor_1 (xor_1_out, register_2_q[1], register_2_q[0]);
  not not_12 (not_12_out, register_2_q[1]);
  and and_10 (and_10_out, not_12_out, register_2_q[0], not_13_out);
  not not_13 (not_13_out, not_15_out[0]);
  and and_11 (and_11_out, register_2_q[1], not_14_out);
  not not_14 (not_14_out, register_2_q[0]);
  and and_12 (and_12_out, register_2_q[1], register_2_q[0], not_15_out[0]);
  not not_15 (not_15_out[0], register_3_q[3]);
  and A_C (xor_1_out, I_O_Enable, not_15_out[0], not_16_out, not_17_out, not_18_out);
  LED led_1 (.in(xor_1_out));
  or or_2 (not_15_out[1], and_10_out, and_11_out, and_12_out);
  and D0 (D0_out, I_O_Enable, not_15_out[0], not_16_out, not_17_out, register_3_q[0]);
  Multiplexer #(.enable("false")) multiplexer_1 (
    .in0(multiplexer_1_out), .in1(D0_out), .out(multiplexer_1_out), .sel(not_15_out[0]));
  LED led_2 (.in(multiplexer_1_out));
  not not_16 (not_16_out, register_3_q[2]);
  and D2 (D2_out, I_O_Enable, not_16_out, register_3_q[1], register_3_q[0]);
  and D1 (D1_out, I_O_Enable, not_15_out[0], not_16_out, register_3_q[1], not_18_out);
  LED led_3 (.in(D1_out));
  LED led_4 (.in(D2_out));
  not not_17 (not_17_out, register_3_q[1]);
  and D3 (D3_out, I_O_Enable, not_15_out[0], register_3_q[2], not_17_out, not_18_out);
  LED led_5 (.in(D3_out));
  not not_18 (not_18_out, register_3_q[0]);
  and Engine (Engine_out, I_O_Enable, not_15_out[0], register_3_q[2], not_17_out, register_3_q[0]);
  LED led_6 (.in(Engine_out));
  and Wipers (Wipers_out, I_O_Enable, register_3_q[2], register_3_q[1], not_18_out);
  LED led_7 (.in(Wipers_out));
  Button Button ();  // open: out
  Register #(.width(1)) register_4 (.D(Wipers_out), .Q(register_3_q[3]), .clk(clock_1_out));  // open: en, clr
  Clock clock_2 (.out(clock_2_out));
  Register #(.width(2)) register_5 (
    .D({or_3_out[1], in_5}), .Q(register_5_q), .clk(clock_2_out), .clr(Reset_2_out));  // open: en
  Button Reset_2 (.out(Reset_2_out));
  not not_19 (not_19_out, register_5_q[1]);
  and and_13 (and_13_out, not_19_out, register_5_q[0], not_20_out);
  not not_20 (not_20_out, in_5);
  and and_14 (and_14_out, register_5_q[1], not_21_out);
  not not_21 (not_21_out, register_5_q[0]);
  and and_15 (and_15_out, register_5_q[1], register_5_q[0], in_5);
  xor xor_2 (xor_2_out, register_5_q[1], register_5_q[0]);
  or or_3 (or_3_out[1], and_13_out, and_14_out, and_15_out);
  LED led_8 (.in(xor_2_out));

  assign out_8 = 1'b0;
  assign out_9 = 1'b0;
  assign out_10 = 1'b0;
  assign out_11 = 1'b0;

  // Notes on the sheet:
  //   D0
  //   S0
  //   S1
  //   D1
  //   D0
  //   S1
  //   S0
  //   D1
endmodule
