// Logisim project Lab3Prob3v2.circ as structural Verilog: 1 circuit, main circuit main
module main (
  input  Enable
);

  wire A_C_off_out, A_C_on_out, A_out, and_1_out, and_2_out, and_3_out, and_4_out, and_5_out, and_6_out,
       and_7_out, B_out, C_out, clock_1_out, D0_off_out, D0_on_out, D1_off_out, D1_on_out, D2_off_out,
       D2_on_out, D3_off_out, D3_on_out, D_out, E_out, Engine_off_out, Engine_on_out, F_out, G_out, H_out,
       I_out, J_out, K_out, L_out, M_out, N_out, not_1_out, not_2_out, not_3_out, not_4_out, not_5_out,
       not_6_out, not_7_out, not_8_out, not_9_out, not_10_out, not_11_out, not_12_out, not_13_out,
       not_14_out, not_15_out, O_out, or_1_out, or_2_out, or_3_out, or_4_out, or_5_out, or_6_out, or_7_out,
       Wipers_off_out, Wipers_on_out;
  wire [3:0] _0_out, register_1_q, register_2_q;

  not not_1 (not_1_out, register_1_q[0]);
  not not_2 (not_2_out, register_1_q[1]);
  not not_3 (not_3_out, register_1_q[2]);
  not not_4 (not_4_out, register_1_q[3]);
  Clock clock_1 (.out(clock_1_out));
  and A (A_out, not_1_out, not_2_out, not_3_out, not_4_out);
  and B (B_out, not_1_out, not_2_out, not_3_out, register_1_q[3]);
  and C (C_out, not_1_out, not_2_out, register_1_q[2], not_4_out);
  and D (D_out, not_1_out, not_2_out, register_1_q[2], register_1_q[3]);
  and E (E_out, not_1_out, register_1_q[1], not_3_out, not_4_out);
  and F (F_out, not_1_out, register_1_q[1], not_3_out, register_1_q[3]);
  and G (G_out, not_1_out, register_1_q[1], register_1_q[2], not_4_out);
  and H (H_out, not_1_out, register_1_q[1], register_1_q[2], register_1_q[3]);
  and I (I_out, register_1_q[0], not_2_out, not_3_out, not_4_out);
  and J (J_out, register_1_q[0], not_2_out, not_3_out, register_1_q[3]);
  and K (K_out, register_1_q[0], not_2_out, register_1_q[2], not_4_out);
  and L (L_out, register_1_q[0], not_2_out, register_1_q[2], register_1_q[3]);
  and M (M_out, register_1_q[0], register_1_q[1], not_3_out, not_4_out);
  and N (N_out, register_1_q[0], register_1_q[1], not_3_out, register_1_q[3]);
  and O (O_out, register_1_q[0], register_1_q[1], register_1_q[2], not_4_out);
  // AND_Gate P has open pins: in0=register_1_q[0], in1=register_1_q[1], in2=register_1_q[2], in3=register_1_q[3], out=open
  Register #(.width(4)) register_1 (
    .D(_0_out), .en(1'b1), .Q({register_1_q[0], register_1_q[1], register_1_q[2], register_1_q[3]}),
    .clk(clock_1_out));  // open: clr
  or _0 (_0_out[0], A_out, C_out, E_out, G_out, I_out, K_out, M_out, O_out);
  or _1 (_0_out[1], B_out, C_out, F_out, G_out, J_out, K_out, N_out, O_out);
  or _2 (_0_out[2], D_out, E_out, F_out, G_out, L_out, M_out, N_out, O_out);
  or _3 (_0_out[3], H_out, I_out, J_out, K_out, L_out, M_out, N_out, O_out);
  Register #(.width(4)) register_2 (.D(register_1_q), .Q(register_2_q), .clk(clock_1_out));  // open: en, clr
  not not_5 (not_5_out, register_2_q[0]);
  not not_6 (not_6_out, register_2_q[1]);
  not not_7 (not_7_out, register_2_q[2]);
  not not_8 (not_8_out, register_2_q[3]);
  and A_C_on (A_C_on_out, not_8_out, not_7_out, not_6_out, not_5_out, Enable);
  and A_C_off (A_C_off_out, not_8_out, not_7_out, not_6_out, register_2_q[0], Enable);
  and D0_on (D0_on_out, register_2_q[3], not_7_out, not_6_out, not_5_out, Enable);
  and D0_off (D0_off_out, register_2_q[3], not_7_out, not_6_out, register_2_q[0], Enable);
  and D1_on (D1_on_out, not_8_out, register_2_q[2], not_6_out, not_5_out, Enable);
  and D1_off (D1_off_out, not_8_out, register_2_q[2], not_6_out, register_2_q[0], Enable);
  and D2_on (D2_on_out, register_2_q[3], register_2_q[2], not_6_out, not_5_out, Enable);
  and D2_off (D2_off_out, register_2_q[3], register_2_q[2], not_6_out, register_2_q[0], Enable);
  and D3_on (D3_on_out, not_8_out, not_7_out, register_2_q[1], not_5_out, Enable);
  and D3_off (D3_off_out, not_8_out, not_7_out, register_2_q[1], register_2_q[0], Enable);
  and Engine_on (Engine_on_out, register_2_q[3], not_7_out, register_2_q[1], not_5_out, Enable);
  and Engine_off (Engine_off_out, register_2_q[3], not_7_out, register_2_q[1], register_2_q[0], Enable);
  and Wipers_on (Wipers_on_out, not_8_out, register_2_q[2], register_2_q[1], not_5_out, Enable);
  and Wipers_off (Wipers_off_out, not_8_out, register_2_q[2], register_2_q[1], register_2_q[0], Enable);
  LED led_1 (.in(and_1_out));
  or or_1 (or_1_out, A_C_on_out, and_1_out);
  not not_9 (not_9_out, A_C_off_out);
  or or_2 (or_2_out, D0_on_out, and_2_out);
  not not_10 (not_10_out, D0_off_out);
  or or_3 (or_3_out, D1_on_out, and_3_out);
  not not_11 (not_11_out, D1_off_out);
  or or_4 (or_4_out, D2_on_out, and_4_out);
  not not_12 (not_12_out, D2_off_out);
  or or_5 (or_5_out, D3_on_out, and_5_out);
  not not_13 (not_13_out, D3_off_out);
  or or_6 (or_6_out, Engine_on_out, and_6_out);
  not not_14 (not_14_out, Engine_off_out);
  or or_7 (or_7_out, Wipers_on_out, and_7_out);
  not not_15 (not_15_out, Wipers_off_out);
  LED led_2 (.in(and_2_out));
  LED led_3 (.in(and_3_out));
  LED led_4 (.in(and_4_out));
  and and_1 (and_1_out, or_1_out, not_9_out);
  and and_2 (and_2_out, or_2_out, not_10_out);
  and and_3 (and_3_out, or_3_out, not_11_out);
  and and_4 (and_4_out, or_4_out, not_12_out);
  and and_5 (and_5_out, or_5_out, not_13_out);
  and and_6 (and_6_out, or_6_out, not_14_out);
  and and_7 (and_7_out, or_7_out, not_15_out);
  LED led_5 (.in(and_7_out));
  LED led_6 (.in(and_5_out));
  LED led_7 (.in(and_6_out));
endmodule
