// Logisim project Lab4_Prob1A.circ as structural Verilog: 1 circuit, main circuit main
module main (
  input  L,
  input  R
);

  wire _0_out, _1_out, _2_out, _3_out, _4_out, _5_out, _6_out, _7_out, _8_out, _9_out, _10_out, _11_out,
       _12_out, _13_out, _14_out, _15_out, _16_out, _17_out, _18_out, _19_out, and_1_out, and_2_out,
       and_3_out, and_4_out, and_5_out, and_6_out, and_7_out, and_8_out, and_9_out, and_10_out, and_11_out,
       and_12_out, and_13_out, and_14_out, and_15_out, and_16_out, and_17_out, and_18_out, and_19_out,
       and_20_out, and_21_out, and_22_out, and_27_out, and_28_out, and_29_out, and_30_out, and_31_out,
       and_32_out, and_33_out, and_34_out, and_35_out, and_36_out, and_37_out, and_38_out, and_39_out,
       and_40_out, and_41_out, and_42_out, and_43_out, and_44_out, and_45_out, and_46_out, and_47_out,
       and_48_out, and_49_out, and_50_out, and_51_out, and_52_out, and_53_out, and_54_out, and_55_out,
       and_56_out, and_57_out, and_58_out, and_59_out, and_60_out, and_61_out, and_62_out, and_63_out,
       and_64_out, and_65_out, and_66_out, and_67_out, and_68_out, and_69_out, and_70_out, and_71_out,
       and_72_out, and_73_out, and_74_out, and_75_out, and_76_out, and_77_out, and_78_out, and_79_out,
       and_80_out, and_81_out, and_82_out, and_83_out, and_84_out, and_85_out, and_86_out, clock_1_out,
       not_2_out, not_4_out, not_5_out, not_6_out, not_7_out, not_8_out, not_9_out, not_10_out, not_11_out,
       not_12_out, not_13_out, not_14_out, not_15_out, not_16_out, not_17_out, not_18_out, not_19_out,
       not_20_out, not_21_out, not_22_out, not_23_out, not_24_out, not_25_out, not_26_out, not_27_out,
       not_28_out, not_29_out, not_30_out, not_31_out, not_32_out, not_33_out, not_34_out, not_35_out,
       not_36_out, not_37_out, not_38_out, not_39_out, not_40_out, not_41_out, not_42_out, not_43_out,
       not_44_out, not_45_out, not_46_out, not_47_out, not_48_out, not_49_out, not_50_out, not_51_out,
       not_52_out, not_53_out, not_54_out, not_55_out, not_56_out, not_57_out, not_58_out, not_59_out,
       not_60_out, not_61_out, not_62_out, not_63_out, not_64_out, not_65_out, not_66_out, not_67_out,
       not_68_out, not_69_out, or_2_out, or_3_out, or_4_out, or_5_out, or_6_out, or_7_out, or_8_out,
       or_9_out, or_10_out, or_11_out, or_12_out, or_13_out, or_14_out, or_15_out, or_16_out, or_17_out,
       or_18_out, or_19_out, or_20_out, or_21_out, or_22_out, or_23_out, or_24_out, or_25_out;
  wire [4:0] not_3_out, register_1_q;
  wire [6:0] register_2_q;
  wire [6:5] not_1_out;

  or or_1 (not_1_out[6], L, R);
  not not_1 (not_1_out[5], R);
  not not_2 (not_2_out, register_1_q[4]);
  not not_3 (not_3_out[0], register_1_q[0]);
  not not_4 (not_4_out, register_1_q[1]);
  not not_5 (not_5_out, register_1_q[3]);
  not not_6 (not_6_out, register_1_q[2]);
  and and_1 (and_1_out, not_2_out, register_1_q[3], register_1_q[2], register_1_q[1], register_1_q[0]);
  and and_2 (and_2_out, register_1_q[4], not_5_out, not_6_out, register_1_q[1], register_1_q[0]);
  and and_3 (and_3_out, register_1_q[3], register_1_q[2], not_4_out, register_1_q[0]);
  and and_4 (and_4_out, register_1_q[3], register_1_q[2], not_4_out, not_3_out[0]);
  and and_5 (and_5_out, not_5_out, register_1_q[2], register_1_q[1], register_1_q[0]);
  and and_6 (and_6_out, register_1_q[3], not_6_out, not_4_out, register_1_q[0]);
  and and_7 (and_7_out, register_1_q[3], not_6_out, register_1_q[1], register_1_q[0]);
  and and_8 (and_8_out, register_1_q[3], register_1_q[2], not_4_out, register_1_q[0]);
  and and_9 (and_9_out, register_1_q[3], not_6_out, not_3_out[0]);
  and and_10 (and_10_out, register_1_q[3], register_1_q[1], not_3_out[0]);
  and and_11 (and_11_out, not_6_out, register_1_q[1], register_1_q[0]);
  and and_12 (and_12_out, register_1_q[2], not_4_out, not_3_out[0]);
  and and_13 (and_13_out, register_1_q[2], not_4_out, register_1_q[0]);
  and and_14 (and_14_out, register_1_q[2], register_1_q[1], not_3_out[0]);
  and and_15 (and_15_out, register_1_q[2], not_4_out, register_1_q[0]);
  and and_16 (and_16_out, not_5_out, register_1_q[1], not_3_out[0]);
  and and_17 (and_17_out, not_5_out, not_6_out, not_4_out, register_1_q[0]);
  and and_18 (and_18_out, not_5_out, register_1_q[2], register_1_q[1], not_3_out[0]);
  and and_19 (and_19_out, register_1_q[3], not_6_out, register_1_q[1], not_3_out[0]);
  and and_20 (and_20_out, register_1_q[3], not_6_out, not_4_out, register_1_q[0]);
  and and_21 (and_21_out, register_1_q[3], register_1_q[2], register_1_q[1], not_3_out[0]);
  and and_22 (and_22_out, register_1_q[4], not_5_out, not_6_out, register_1_q[1], register_1_q[0]);
  or or_2 (or_2_out, register_1_q[4], and_1_out);
  and and_23 (not_3_out[4], or_2_out, not_7_out);
  not not_7 (not_7_out, and_2_out);
  not not_8 (not_8_out, and_22_out);
  Register #(.width(5)) register_1 (.D(not_3_out), .en(1'b1), .Q(register_1_q), .clk(clock_1_out));  // open: clr
  Clock clock_1 (.out(clock_1_out));
  or or_3 (or_3_out, and_3_out, and_4_out, and_5_out, and_6_out, and_7_out, and_8_out, and_9_out, and_10_out);
  or or_4 (or_4_out, and_11_out, and_12_out, and_13_out, and_14_out);
  or or_5 (or_5_out, and_15_out, and_16_out, and_17_out, and_18_out, and_19_out, and_20_out, and_21_out);
  and and_24 (not_3_out[3], or_3_out, not_8_out);
  and and_25 (not_3_out[2], or_4_out, not_8_out);
  and and_26 (not_3_out[1], or_5_out, not_8_out);
  Register #(.width(7)) register_2 (
    .D({not_1_out, register_1_q[0], register_1_q[1], register_1_q[2], register_1_q[3], register_1_q[4]}),
    .en(1'b1), .Q(register_2_q), .clk(clock_1_out));  // open: clr
  and and_27 (and_27_out, or_6_out, register_2_q[6]);
  LED led_1 (.in(and_27_out));
  and and_28 (and_28_out, or_7_out, register_2_q[6]);
  and and_29 (and_29_out, or_8_out, register_2_q[6]);
  LED led_2 (.in(and_28_out));
  LED led_3 (.in(and_29_out));
  and and_30 (and_30_out, or_9_out, register_2_q[6]);
  LED led_4 (.in(and_30_out));
  and and_31 (and_31_out, or_11_out, register_2_q[6]);
  and and_32 (and_32_out, or_10_out, register_2_q[6]);
  LED led_5 (.in(and_31_out));
  LED led_6 (.in(and_32_out));
  and and_33 (and_33_out, or_12_out, register_2_q[6]);
  and and_34 (and_34_out, or_13_out, register_2_q[6]);
  LED led_7 (.in(and_33_out));
  LED led_8 (.in(and_34_out));
  not not_9 (not_9_out, register_2_q[4]);
  not not_10 (not_10_out, register_2_q[3]);
  and _0 (_0_out, not_9_out, not_10_out, not_11_out, not_12_out, not_13_out);
  not not_11 (not_11_out, register_2_q[2]);
  not not_12 (not_12_out, register_2_q[1]);
  not not_13 (not_13_out, register_2_q[0]);
  not not_14 (not_14_out, register_2_q[3]);
  not not_15 (not_15_out, register_2_q[2]);
  and _1 (_1_out, register_2_q[4], not_14_out, not_15_out, not_16_out, not_17_out);
  not not_16 (not_16_out, register_2_q[1]);
  not not_17 (not_17_out, register_2_q[0]);
  not not_18 (not_18_out, register_2_q[4]);
  and _2 (_2_out, not_18_out, register_2_q[3], not_19_out, not_20_out, not_21_out);
  not not_19 (not_19_out, register_2_q[2]);
  not not_20 (not_20_out, register_2_q[1]);
  not not_21 (not_21_out, register_2_q[0]);
  not not_22 (not_22_out, register_2_q[2]);
  and _3 (_3_out, register_2_q[4], register_2_q[3], not_22_out, not_23_out, not_24_out);
  not not_23 (not_23_out, register_2_q[1]);
  not not_24 (not_24_out, register_2_q[0]);
  not not_25 (not_25_out, register_2_q[4]);
  not not_26 (not_26_out, register_2_q[3]);
  and _4 (_4_out, not_25_out, not_26_out, register_2_q[2], not_27_out, not_28_out);
  not not_27 (not_27_out, register_2_q[1]);
  not not_28 (not_28_out, register_2_q[0]);
  not not_29 (not_29_out, register_2_q[3]);
  and _5 (_5_out, register_2_q[4], not_29_out, register_2_q[2], not_30_out, not_31_out);
  not not_30 (not_30_out, register_2_q[1]);
  not not_31 (not_31_out, register_2_q[0]);
  not not_32 (not_32_out, register_2_q[4]);
  and _6 (_6_out, not_32_out, register_2_q[3], register_2_q[2], not_33_out, not_34_out);
  not not_33 (not_33_out, register_2_q[1]);
  not not_34 (not_34_out, register_2_q[0]);
  and _7 (_7_out, register_2_q[4], register_2_q[3], register_2_q[2], not_35_out, not_36_out);
  not not_35 (not_35_out, register_2_q[1]);
  not not_36 (not_36_out, register_2_q[0]);
  not not_37 (not_37_out, register_2_q[4]);
  not not_38 (not_38_out, register_2_q[3]);
  and _8 (_8_out, not_37_out, not_38_out, not_39_out, register_2_q[1], not_40_out);
  not not_39 (not_39_out, register_2_q[2]);
  not not_40 (not_40_out, register_2_q[0]);
  not not_41 (not_41_out, register_2_q[3]);
  and _9 (_9_out, register_2_q[4], not_41_out, not_42_out, register_2_q[1], not_43_out);
  not not_42 (not_42_out, register_2_q[2]);
  not not_43 (not_43_out, register_2_q[0]);
  not not_44 (not_44_out, register_2_q[4]);
  and _10 (_10_out, not_44_out, register_2_q[3], not_45_out, register_2_q[1], not_46_out);
  not not_45 (not_45_out, register_2_q[2]);
  not not_46 (not_46_out, register_2_q[0]);
  and _11 (_11_out, register_2_q[4], register_2_q[3], not_47_out, register_2_q[1], not_48_out);
  not not_47 (not_47_out, register_2_q[2]);
  not not_48 (not_48_out, register_2_q[0]);
  not not_49 (not_49_out, register_2_q[4]);
  not not_50 (not_50_out, register_2_q[3]);
  and _12 (_12_out, not_49_out, not_50_out, register_2_q[2], register_2_q[1], not_51_out);
  not not_51 (not_51_out, register_2_q[0]);
  not not_52 (not_52_out, register_2_q[3]);
  and _13 (_13_out, register_2_q[4], not_52_out, register_2_q[2], register_2_q[1], not_53_out);
  not not_53 (not_53_out, register_2_q[0]);
  not not_54 (not_54_out, register_2_q[4]);
  and _14 (_14_out, not_54_out, register_2_q[3], register_2_q[2], register_2_q[1], not_55_out);
  not not_55 (not_55_out, register_2_q[0]);
  and _15 (_15_out, register_2_q[4], register_2_q[3], register_2_q[2], register_2_q[1], not_56_out);
  not not_56 (not_56_out, register_2_q[0]);
  not not_57 (not_57_out, register_2_q[4]);
  not not_58 (not_58_out, register_2_q[3]);
  not not_59 (not_59_out, register_2_q[2]);
  and _16 (_16_out, not_57_out, not_58_out, not_59_out, not_60_out, register_2_q[0]);
  not not_60 (not_60_out, register_2_q[1]);
  not not_61 (not_61_out, register_2_q[3]);
  not not_62 (not_62_out, register_2_q[2]);
  and _17 (_17_out, register_2_q[4], not_61_out, not_62_out, not_63_out, register_2_q[0]);
  not not_63 (not_63_out, register_2_q[1]);
  not not_64 (not_64_out, register_2_q[4]);
  not not_65 (not_65_out, register_2_q[2]);
  and _18 (_18_out, not_64_out, register_2_q[3], not_65_out, not_66_out, register_2_q[0]);
  not not_66 (not_66_out, register_2_q[1]);
  not not_67 (not_67_out, register_2_q[2]);
  and _19 (_19_out, register_2_q[4], register_2_q[3], not_67_out, not_68_out, register_2_q[0]);
  not not_68 (not_68_out, register_2_q[1]);
  and and_35 (and_35_out, or_14_out, register_2_q[6]);
  LED led_9 (.in(and_35_out));
  and and_36 (and_36_out, or_16_out, register_2_q[6]);
  and and_37 (and_37_out, or_15_out, register_2_q[6]);
  LED led_10 (.in(and_36_out));
  LED led_11 (.in(and_37_out));
  and and_38 (and_38_out, or_17_out, register_2_q[6]);
  LED led_12 (.in(and_38_out));
  and and_39 (and_39_out, or_19_out, register_2_q[6]);
  and and_40 (and_40_out, or_18_out, register_2_q[6]);
  LED led_13 (.in(and_40_out));
  LED led_14 (.in(and_39_out));
  and and_41 (and_41_out, register_2_q[5], _19_out);
  and and_42 (and_42_out, register_2_q[5], _18_out);
  and and_43 (and_43_out, register_2_q[5], _17_out);
  and and_44 (and_44_out, register_2_q[5], _16_out);
  and and_45 (and_45_out, register_2_q[5], _15_out);
  and and_46 (and_46_out, register_2_q[5], _14_out);
  and and_47 (and_47_out, register_2_q[5], _13_out);
  and and_48 (and_48_out, register_2_q[5], _12_out);
  and and_49 (and_49_out, register_2_q[5], _11_out);
  and and_50 (and_50_out, register_2_q[5], _10_out);
  and and_51 (and_51_out, register_2_q[5], _9_out);
  and and_52 (and_52_out, register_2_q[5], _8_out);
  and and_53 (and_53_out, register_2_q[5], _7_out);
  and and_54 (and_54_out, register_2_q[5], _6_out);
  and and_55 (and_55_out, register_2_q[5], _5_out);
  and and_56 (and_56_out, register_2_q[5], _4_out);
  and and_57 (and_57_out, register_2_q[5], _3_out);
  and and_58 (and_58_out, register_2_q[5], _2_out);
  and and_59 (and_59_out, register_2_q[5], _1_out);
  and and_60 (and_60_out, register_2_q[5], _0_out);
  and and_61 (and_61_out, or_20_out, register_2_q[6]);
  and and_62 (and_62_out, or_21_out, register_2_q[6]);
  LED led_15 (.in(and_62_out));
  LED led_16 (.in(and_61_out));
  not not_69 (not_69_out, register_2_q[5]);
  and and_63 (and_63_out, not_69_out, _0_out);
  and and_64 (and_64_out, not_69_out, _0_out);
  and and_65 (and_65_out, not_69_out, _2_out);
  and and_66 (and_66_out, not_69_out, _3_out);
  and and_67 (and_67_out, not_69_out, _4_out);
  and and_68 (and_68_out, not_69_out, _5_out);
  and and_69 (and_69_out, not_69_out, _6_out);
  and and_70 (and_70_out, not_69_out, _7_out);
  and and_71 (and_71_out, not_69_out, _8_out);
  and and_72 (and_72_out, not_69_out, _9_out);
  and and_73 (and_73_out, not_69_out, _10_out);
  and and_74 (and_74_out, not_69_out, _11_out);
  and and_75 (and_75_out, not_69_out, _12_out);
  and and_76 (and_76_out, not_69_out, _13_out);
  and and_77 (and_77_out, not_69_out, _14_out);
  and and_78 (and_78_out, not_69_out, _15_out);
  and and_79 (and_79_out, not_69_out, _16_out);
  and and_80 (and_80_out, not_69_out, _17_out);
  and and_81 (and_81_out, not_69_out, _18_out);
  and and_82 (and_82_out, not_69_out, _19_out);
  and and_83 (and_83_out, or_22_out, register_2_q[6]);
  LED led_17 (.in(and_83_out));
  and and_84 (and_84_out, or_24_out, register_2_q[6]);
  and and_85 (and_85_out, or_23_out, register_2_q[6]);
  LED led_18 (.in(and_85_out));
  LED led_19 (.in(and_84_out));
  or or_6 (or_6_out, and_41_out, and_63_out);
  or or_7 (or_7_out, and_42_out, and_64_out);
  or or_8 (or_8_out, and_43_out, and_65_out);
  or or_9 (or_9_out, and_44_out, and_66_out);
  or or_10 (or_10_out, and_45_out, and_67_out);
  or or_11 (or_11_out, and_46_out, and_68_out);
  or or_12 (or_12_out, and_47_out, and_69_out);
  or or_13 (or_13_out, and_48_out, and_70_out);
  or or_14 (or_14_out, and_49_out, and_71_out);
  or or_15 (or_15_out, and_50_out, and_72_out);
  or or_16 (or_16_out, and_51_out, and_73_out);
  or or_17 (or_17_out, and_52_out, and_74_out);
  or or_18 (or_18_out, and_53_out, and_75_out);
  or or_19 (or_19_out, and_54_out, and_76_out);
  or or_20 (or_20_out, and_55_out, and_77_out);
  or or_21 (or_21_out, and_56_out, and_78_out);
  or or_22 (or_22_out, and_57_out, and_79_out);
  or or_23 (or_23_out, and_58_out, and_80_out);
  or or_24 (or_24_out, and_59_out, and_81_out);
  or or_25 (or_25_out, and_60_out, and_82_out);
  and and_86 (and_86_out, or_25_out, register_2_q[6]);
  LED led_20 (.in(and_86_out));

  // Notes on the sheet:
  //   BUS
endmodule
