// Logisim project Lab4_Prob3A.circ as structural Verilog: 1 circuit, main circuit main
module main (
  input  [7:0] in_1,
  input  [7:0] in_2,
  output [8:0] out_3
);

  wire and_1_out, and_2_out, and_3_out, and_4_out, and_5_out, and_6_out, and_7_out, and_8_out, and_9_out,
       and_10_out, and_11_out, and_12_out, and_13_out, and_14_out, and_15_out, clock_1_out, or_1_out,
       or_2_out, or_3_out, or_4_out, or_5_out, or_6_out, xor_2_out, xor_4_out, xor_6_out, xor_8_out,
       xor_10_out, xor_12_out, xor_14_out;
  wire [7:0] register_1_q, register_2_q;

  Clock clock_1 (.out(clock_1_out));
  Register register_1 (.D(in_1), .Q(register_1_q), .clk(clock_1_out));  // open: en, clr
  Register register_2 (.D(in_2), .Q(register_2_q), .clk(clock_1_out));  // open: en, clr
  xor xor_1 (out_3[0], register_2_q[0], register_1_q[0]);
  and and_1 (and_1_out, register_2_q[0], register_1_q[0]);
  and and_2 (and_2_out, register_2_q[1], register_1_q[1]);
  xor xor_2 (xor_2_out, register_2_q[1], register_1_q[1]);
  and and_3 (and_3_out, and_1_out, xor_2_out);
  or or_1 (or_1_out, and_2_out, and_3_out);
  and and_4 (and_4_out, register_2_q[2], register_1_q[2]);
  and and_5 (and_5_out, or_1_out, xor_4_out);
  or or_2 (or_2_out, and_4_out, and_5_out);
  and and_6 (and_6_out, register_2_q[3], register_1_q[3]);
  or or_3 (or_3_out, and_6_out, and_7_out);
  xor xor_3 (out_3[1], and_1_out, xor_2_out);
  xor xor_4 (xor_4_out, register_2_q[2], register_1_q[2]);
  xor xor_5 (out_3[2], or_1_out, xor_4_out);
  xor xor_6 (xor_6_out, register_2_q[3], register_1_q[3]);
  and and_7 (and_7_out, or_2_out, xor_6_out);
  xor xor_7 (out_3[3], or_2_out, xor_6_out);
  xor xor_8 (xor_8_out, register_2_q[4], register_1_q[4]);
  and and_8 (and_8_out, register_2_q[4], register_1_q[4]);
  and and_9 (and_9_out, or_3_out, xor_8_out);
  or or_4 (or_4_out, and_8_out, and_9_out);
  and and_10 (and_10_out, register_2_q[5], register_1_q[5]);
  or or_5 (or_5_out, and_10_out, and_11_out);
  xor xor_9 (out_3[4], or_3_out, xor_8_out);
  xor xor_10 (xor_10_out, register_2_q[5], register_1_q[5]);
  and and_11 (and_11_out, or_4_out, xor_10_out);
  xor xor_11 (out_3[5], or_4_out, xor_10_out);
  xor xor_12 (xor_12_out, register_2_q[6], register_1_q[6]);
  and and_12 (and_12_out, register_2_q[6], register_1_q[6]);
  and and_13 (and_13_out, or_5_out, xor_12_out);
  or or_6 (or_6_out, and_12_out, and_13_out);
  xor xor_13 (out_3[6], or_5_out, xor_12_out);
  and and_14 (and_14_out, register_2_q[7], register_1_q[7]);
  xor xor_14 (xor_14_out, register_2_q[7], register_1_q[7]);
  and and_15 (and_15_out, or_6_out, xor_14_out);
  or or_7 (out_3[8], and_14_out, and_15_out);
  xor xor_15 (out_3[7], or_6_out, xor_14_out);

  // Notes on the sheet:
  //   HA-0
  //   FA-1
  //   FA-2
  //   FA-3
  //   FA-4
  //   FA-5
  //   FA-6
  //   FA-7
endmodule
