// Logisim project Lab4_Prob3B.circ as structural Verilog: 1 circuit, main circuit main
module main (
  input  [7:0] in_1,
  input  [7:0] in_2,
  output [7:0] COMPUTES_B_A
);

  wire clock_1_out, nand_1_out, nand_2_out, nand_3_out, nand_4_out, nand_5_out, nand_6_out, nand_7_out,
       nand_8_out, nand_9_out, nand_10_out, nand_11_out, nand_12_out, nand_13_out, nand_14_out, nand_15_out,
       nand_16_out, not_1_out, not_2_out, not_3_out, or_1_out, or_2_out, or_3_out, or_4_out, or_5_out,
       or_6_out, or_7_out, xor_1_out, xor_2_out, xor_3_out, xor_7_out, xor_9_out, xor_11_out, xor_13_out,
       xor_15_out;
  wire [7:0] register_1_q, register_2_q;

  Clock clock_1 (.out(clock_1_out));
  Register register_1 (.D(in_1), .Q(register_1_q), .clk(clock_1_out));  // open: en, clr
  Register register_2 (.D(in_2), .Q(register_2_q), .clk(clock_1_out));  // open: en, clr
  nand nand_1 (nand_1_out, register_2_q[0], not_1_out);
  not not_1 (not_1_out, register_1_q[0]);
  xor xor_1 (xor_1_out, register_2_q[0], not_1_out);
  not nand_2 (nand_2_out, xor_1_out);  // NAND_Gate
  or or_1 (or_1_out, ~nand_1_out, ~nand_2_out);  // OR_Gate
  not not_2 (not_2_out, register_1_q[1]);
  xor xor_2 (xor_2_out, register_2_q[1], not_2_out);
  nand nand_3 (nand_3_out, register_2_q[1], not_2_out);
  nand nand_4 (nand_4_out, or_1_out, xor_2_out);
  or or_2 (or_2_out, ~nand_3_out, ~nand_4_out);  // OR_Gate
  xor xor_3 (xor_3_out, register_2_q[2], not_3_out);
  nand nand_5 (nand_5_out, register_2_q[2], not_3_out);
  nand nand_6 (nand_6_out, or_2_out, xor_3_out);
  or or_3 (or_3_out, ~nand_5_out, ~nand_6_out);  // OR_Gate
  nand nand_7 (nand_7_out, register_2_q[3], ~register_1_q[3]);  // NAND_Gate
  or or_4 (or_4_out, ~nand_7_out, ~nand_8_out);  // OR_Gate
  xor xor_4 (COMPUTES_B_A[0], 1'b1, xor_1_out);
  xor xor_5 (COMPUTES_B_A[1], or_1_out, xor_2_out);
  not not_3 (not_3_out, register_1_q[2]);
  xor xor_6 (COMPUTES_B_A[2], or_2_out, xor_3_out);
  xor xor_7 (xor_7_out, register_2_q[3], ~register_1_q[3]);  // XOR_Gate
  nand nand_8 (nand_8_out, or_3_out, xor_7_out);
  xor xor_8 (COMPUTES_B_A[3], or_3_out, xor_7_out);
  xor xor_9 (xor_9_out, register_2_q[4], ~register_1_q[4]);  // XOR_Gate
  nand nand_9 (nand_9_out, register_2_q[4], ~register_1_q[4]);  // NAND_Gate
  nand nand_10 (nand_10_out, or_4_out, xor_9_out);
  or or_5 (or_5_out, ~nand_9_out, ~nand_10_out);  // OR_Gate
  nand nand_11 (nand_11_out, register_2_q[5], ~register_1_q[5]);  // NAND_Gate
  or or_6 (or_6_out, ~nand_11_out, ~nand_12_out);  // OR_Gate
  xor xor_10 (COMPUTES_B_A[4], or_4_out, xor_9_out);
  xor xor_11 (xor_11_out, register_2_q[5], ~register_1_q[5]);  // XOR_Gate
  nand nand_12 (nand_12_out, or_5_out, xor_11_out);
  xor xor_12 (COMPUTES_B_A[5], or_5_out, xor_11_out);
  xor xor_13 (xor_13_out, register_2_q[6], ~register_1_q[6]);  // XOR_Gate
  nand nand_13 (nand_13_out, register_2_q[6], ~register_1_q[6]);  // NAND_Gate
  nand nand_14 (nand_14_out, or_6_out, xor_13_out);
  or or_7 (or_7_out, ~nand_13_out, ~nand_14_out);  // OR_Gate
  nand nand_15 (nand_15_out, register_2_q[7], ~register_1_q[7]);  // NAND_Gate
  xor xor_14 (COMPUTES_B_A[6], or_6_out, xor_13_out);
  xor xor_15 (xor_15_out, register_2_q[7], ~register_1_q[7]);  // XOR_Gate
  nand nand_16 (nand_16_out, or_7_out, xor_15_out);
  // OR_Gate or_8 has open pins: in0=nand_15_out, in1=nand_16_out, out=open
  xor xor_16 (COMPUTES_B_A[7], or_7_out, xor_15_out);

  // Notes on the sheet:
  //   A
  //   B
  //   HS-0
  //   FS-1
  //   FS-2
  //   FS-3
  //   FS-4
  //   FS-5
  //   FS-6
  //   IF NEGATIVE, RETURNS COMPLEMENT
  //   FS-7
endmodule
