// Logisim project Lab4_Prob3C.circ as structural Verilog: 1 circuit, main circuit main
module main (
  input  [7:0] A,
  input  [7:0] B
);

  wire and_1_out, and_2_out, and_3_out, and_4_out, and_5_out, and_6_out, and_7_out, and_8_out, and_9_out,
       and_10_out, and_11_out, and_12_out, and_13_out, and_14_out, and_15_out, and_16_out, and_17_out,
       and_18_out, and_19_out, and_20_out, and_21_out, and_22_out, and_23_out, and_24_out, clock_1_out,
       or_1_out, or_2_out, or_3_out, or_4_out, or_5_out, or_6_out, or_7_out, or_8_out, or_9_out, or_10_out,
       or_11_out, or_12_out, or_13_out, or_14_out, or_15_out, or_16_out, xnor_1_out, xnor_2_out, xnor_3_out,
       xnor_4_out, xnor_5_out, xnor_6_out, xnor_7_out, xnor_8_out;
  wire [7:0] register_1_q, register_2_q;

  and and_1 (and_1_out, register_1_q[7], ~register_2_q[7], 1'b1);  // AND_Gate
  and and_2 (and_2_out, ~register_1_q[7], register_2_q[7], 1'b1);  // AND_Gate
  xnor xnor_1 (xnor_1_out, register_2_q[7], register_1_q[7]);
  or or_1 (or_1_out, and_1_out, 1'b0);
  or or_2 (or_2_out, and_2_out, 1'b0);
  and and_3 (and_3_out, xnor_1_out, 1'b1);
  and and_4 (and_4_out, register_1_q[6], ~register_2_q[6], and_3_out);  // AND_Gate
  and and_5 (and_5_out, ~register_1_q[6], register_2_q[6], and_3_out);  // AND_Gate
  xnor xnor_2 (xnor_2_out, register_2_q[6], register_1_q[6]);
  or or_3 (or_3_out, and_4_out, or_1_out);
  or or_4 (or_4_out, and_5_out, or_2_out);
  and and_6 (and_6_out, xnor_2_out, and_3_out);
  and and_7 (and_7_out, register_1_q[5], ~register_2_q[5], and_6_out);  // AND_Gate
  and and_8 (and_8_out, ~register_1_q[5], register_2_q[5], and_6_out);  // AND_Gate
  or or_5 (or_5_out, and_7_out, or_3_out);
  or or_6 (or_6_out, and_8_out, or_4_out);
  xnor xnor_3 (xnor_3_out, register_2_q[5], register_1_q[5]);
  and and_9 (and_9_out, xnor_3_out, and_6_out);
  Register register_1 (.D(A), .Q(register_1_q), .clk(clock_1_out));  // open: en, clr
  and and_10 (and_10_out, register_1_q[4], ~register_2_q[4], and_9_out);  // AND_Gate
  or or_7 (or_7_out, and_10_out, or_5_out);
  and and_11 (and_11_out, ~register_1_q[4], register_2_q[4], and_9_out);  // AND_Gate
  or or_8 (or_8_out, and_11_out, or_6_out);
  xnor xnor_4 (xnor_4_out, register_2_q[4], register_1_q[4]);
  and and_12 (and_12_out, xnor_4_out, and_9_out);
  Clock clock_1 (.out(clock_1_out));
  Register register_2 (.D(B), .Q(register_2_q), .clk(clock_1_out));  // open: en, clr
  and and_13 (and_13_out, register_1_q[3], ~register_2_q[3], and_12_out);  // AND_Gate
  or or_9 (or_9_out, and_13_out, or_7_out);
  and and_14 (and_14_out, ~register_1_q[3], register_2_q[3], and_12_out);  // AND_Gate
  or or_10 (or_10_out, and_14_out, or_8_out);
  xnor xnor_5 (xnor_5_out, register_2_q[3], register_1_q[3]);
  and and_15 (and_15_out, xnor_5_out, and_12_out);
  and and_16 (and_16_out, register_1_q[2], ~register_2_q[2], and_15_out);  // AND_Gate
  or or_11 (or_11_out, and_16_out, or_9_out);
  and and_17 (and_17_out, ~register_1_q[2], register_2_q[2], and_15_out);  // AND_Gate
  or or_12 (or_12_out, and_17_out, or_10_out);
  xnor xnor_6 (xnor_6_out, register_2_q[2], register_1_q[2]);
  and and_18 (and_18_out, xnor_6_out, and_15_out);
  and and_19 (and_19_out, register_1_q[1], ~register_2_q[1], and_18_out);  // AND_Gate
  or or_13 (or_13_out, and_19_out, or_11_out);
  and and_20 (and_20_out, ~register_1_q[1], register_2_q[1], and_18_out);  // AND_Gate
  or or_14 (or_14_out, and_20_out, or_12_out);
  xnor xnor_7 (xnor_7_out, register_2_q[1], register_1_q[1]);
  and and_21 (and_21_out, xnor_7_out, and_18_out);
  and and_22 (and_22_out, register_1_q[0], ~register_2_q[0], and_21_out);  // AND_Gate
  or or_15 (or_15_out, and_22_out, or_13_out);
  and and_23 (and_23_out, ~register_1_q[0], register_2_q[0], and_21_out);  // AND_Gate
  or or_16 (or_16_out, and_23_out, or_14_out);
  xnor xnor_8 (xnor_8_out, register_2_q[0], register_1_q[0]);
  LED led_1 (.in(or_15_out));
  LED led_2 (.in(or_16_out));
  and and_24 (and_24_out, xnor_8_out, and_21_out);
  LED led_3 (.in(and_24_out));

  // Notes on the sheet:
  //   A > B
  //   A < B
  //   A = B
endmodule
