// Logisim project Lab4_Prob3D.circ as structural Verilog: 1 circuit, main circuit main
module main (
  input  [7:0] in_1,
  input  _1___R___0___L,
  input  in_3,
  input  in_4,
  input  in_5,
  output [7:0] out_6
);

  wire clock_1_out, multiplexer_3_out, multiplexer_4_out, multiplexer_5_out, multiplexer_6_out,
       multiplexer_7_out, multiplexer_8_out, multiplexer_9_out, multiplexer_10_out, multiplexer_11_out,
       multiplexer_12_out, multiplexer_13_out, multiplexer_14_out, multiplexer_15_out, multiplexer_16_out,
       multiplexer_17_out, multiplexer_18_out, not_1_out;
  wire [7:0] multiplexer_1_out, multiplexer_19_out, register_1_q;

  Multiplexer #(.width(8)) multiplexer_1 (
    .in0({in_1[0], in_1[1], in_1[2], in_1[3], in_1[4], in_1[5], in_1[6], in_1[7]}), .in1(in_1),
    .out(multiplexer_1_out), .sel(_1___R___0___L));  // open: en
  Multiplexer #(.width(8)) multiplexer_2 (
    .in0(multiplexer_19_out),
    .in1({multiplexer_19_out[0], multiplexer_19_out[1], multiplexer_19_out[2], multiplexer_19_out[3], multiplexer_19_out[4], multiplexer_19_out[5], multiplexer_19_out[6], multiplexer_19_out[7]}),
    .out(out_6), .sel(_1___R___0___L));  // open: en
  Clock clock_1 (.out(clock_1_out));
  Register register_1 (.D(multiplexer_1_out), .Q(register_1_q), .clk(clock_1_out));  // open: en, clr
  not not_1 (not_1_out, 1'b1);
  Multiplexer multiplexer_3 (
    .in0(register_1_q[0]), .in1(register_1_q[1]), .out(multiplexer_3_out), .sel(in_3));  // open: en
  Multiplexer multiplexer_4 (
    .in0(register_1_q[1]), .in1(register_1_q[2]), .out(multiplexer_4_out), .sel(in_3));  // open: en
  Multiplexer multiplexer_5 (
    .in0(register_1_q[2]), .in1(register_1_q[3]), .out(multiplexer_5_out), .sel(in_3));  // open: en
  Multiplexer multiplexer_6 (
    .in0(register_1_q[3]), .in1(register_1_q[4]), .out(multiplexer_6_out), .sel(in_3));  // open: en
  Multiplexer multiplexer_7 (
    .in0(register_1_q[4]), .in1(register_1_q[5]), .out(multiplexer_7_out), .sel(in_3));  // open: en
  Multiplexer multiplexer_8 (
    .in0(register_1_q[5]), .in1(register_1_q[6]), .out(multiplexer_8_out), .sel(in_3));  // open: en
  Multiplexer multiplexer_9 (
    .in0(register_1_q[6]), .in1(register_1_q[7]), .out(multiplexer_9_out), .sel(in_3));  // open: en
  Multiplexer multiplexer_10 (
    .in0(register_1_q[7]), .in1(not_1_out), .out(multiplexer_10_out), .sel(in_3));  // open: en
  Multiplexer multiplexer_11 (
    .in0(multiplexer_3_out), .in1(multiplexer_5_out), .out(multiplexer_11_out), .sel(in_4));  // open: en
  Multiplexer multiplexer_12 (
    .in0(multiplexer_4_out), .in1(multiplexer_6_out), .out(multiplexer_12_out), .sel(in_4));  // open: en
  Multiplexer multiplexer_13 (
    .in0(multiplexer_5_out), .in1(multiplexer_7_out), .out(multiplexer_13_out), .sel(in_4));  // open: en
  Multiplexer multiplexer_14 (
    .in0(multiplexer_6_out), .in1(multiplexer_8_out), .out(multiplexer_14_out), .sel(in_4));  // open: en
  Multiplexer multiplexer_15 (
    .in0(multiplexer_7_out), .in1(multiplexer_9_out), .out(multiplexer_15_out), .sel(in_4));  // open: en
  Multiplexer multiplexer_16 (
    .in0(multiplexer_8_out), .in1(multiplexer_10_out), .out(multiplexer_16_out), .sel(in_4));  // open: en
  Multiplexer multiplexer_17 (
    .in0(multiplexer_9_out), .in1(not_1_out), .out(multiplexer_17_out), .sel(in_4));  // open: en
  Multiplexer multiplexer_18 (
    .in0(multiplexer_10_out), .in1(not_1_out), .out(multiplexer_18_out), .sel(in_4));  // open: en
  Multiplexer multiplexer_19 (
    .in0(multiplexer_11_out), .in1(multiplexer_15_out), .out(multiplexer_19_out[7]), .sel(in_5));  // open: en
  Multiplexer multiplexer_20 (
    .in0(multiplexer_12_out), .in1(multiplexer_16_out), .out(multiplexer_19_out[6]), .sel(in_5));  // open: en
  Multiplexer multiplexer_21 (
    .in0(multiplexer_13_out), .in1(multiplexer_17_out), .out(multiplexer_19_out[5]), .sel(in_5));  // open: en
  Multiplexer multiplexer_22 (
    .in0(multiplexer_14_out), .in1(multiplexer_18_out), .out(multiplexer_19_out[4]), .sel(in_5));  // open: en
  Multiplexer multiplexer_23 (
    .in0(multiplexer_15_out), .in1(not_1_out), .out(multiplexer_19_out[3]), .sel(in_5));  // open: en
  Multiplexer multiplexer_24 (
    .in0(multiplexer_16_out), .in1(not_1_out), .out(multiplexer_19_out[2]), .sel(in_5));  // open: en
  Multiplexer multiplexer_25 (
    .in0(multiplexer_17_out), .in1(not_1_out), .out(multiplexer_19_out[1]), .sel(in_5));  // open: en
  Multiplexer multiplexer_26 (
    .in0(multiplexer_18_out), .in1(not_1_out), .out(multiplexer_19_out[0]), .sel(in_5));  // open: en
endmodule
