// Logisim project Lab4_Problem1B.circ as structural Verilog: 1 circuit, main circuit main
module main (
  input  L,
  input  R
);

  wire and_1_out, and_2_out, and_3_out, and_4_out, and_5_out, and_6_out, and_7_out, and_8_out, and_9_out,
       and_10_out, and_11_out, and_12_out, and_13_out, and_14_out, and_15_out, and_16_out, and_17_out,
       and_18_out, and_19_out, and_20_out, and_21_out, and_22_out, clock_1_out, not_1_out, not_2_out,
       not_3_out, not_4_out, not_5_out, not_6_out, not_7_out, or_2_out, or_3_out, or_4_out, or_5_out;
  wire [4:0] and_24_out, register_1_q;
  wire [6:0] register_2_q;
  wire [6:6] or_1_out;
  wire [19:0] rom_1_data;

  or or_1 (or_1_out[6], L, R);
  not not_1 (not_1_out, register_1_q[4]);
  not not_2 (not_2_out, register_1_q[2]);
  not not_3 (not_3_out, register_1_q[3]);
  not not_4 (not_4_out, register_1_q[1]);
  not not_5 (not_5_out, register_1_q[0]);
  and and_1 (and_1_out, not_1_out, register_1_q[3], register_1_q[2], register_1_q[1], register_1_q[0]);
  and and_2 (and_2_out, register_1_q[4], not_3_out, not_2_out, register_1_q[1], register_1_q[0]);
  and and_3 (and_3_out, register_1_q[3], register_1_q[2], not_4_out, register_1_q[0]);
  and and_4 (and_4_out, register_1_q[3], register_1_q[2], not_4_out, not_5_out);
  and and_5 (and_5_out, not_3_out, register_1_q[2], register_1_q[1], register_1_q[0]);
  and and_6 (and_6_out, register_1_q[3], not_2_out, not_4_out, register_1_q[0]);
  and and_7 (and_7_out, register_1_q[3], not_2_out, register_1_q[1], register_1_q[0]);
  and and_8 (and_8_out, register_1_q[3], register_1_q[2], not_4_out, register_1_q[0]);
  and and_9 (and_9_out, register_1_q[3], not_2_out, not_5_out);
  and and_10 (and_10_out, register_1_q[3], register_1_q[1], not_5_out);
  and and_11 (and_11_out, not_2_out, register_1_q[1], register_1_q[0]);
  and and_12 (and_12_out, register_1_q[2], not_4_out, not_5_out);
  and and_13 (and_13_out, register_1_q[2], not_4_out, register_1_q[0]);
  and and_14 (and_14_out, register_1_q[2], register_1_q[1], not_5_out);
  and and_15 (and_15_out, register_1_q[2], not_4_out, register_1_q[0]);
  and and_16 (and_16_out, not_3_out, register_1_q[1], not_5_out);
  and and_17 (and_17_out, not_3_out, not_2_out, not_4_out, register_1_q[0]);
  and and_18 (and_18_out, not_3_out, register_1_q[2], register_1_q[1], not_5_out);
  and and_19 (and_19_out, register_1_q[3], not_2_out, register_1_q[1], not_5_out);
  and and_20 (and_20_out, register_1_q[3], not_2_out, not_4_out, register_1_q[0]);
  and and_21 (and_21_out, register_1_q[3], register_1_q[2], register_1_q[1], not_5_out);
  and and_22 (and_22_out, register_1_q[4], not_3_out, not_2_out, register_1_q[1], register_1_q[0]);
  or or_2 (or_2_out, register_1_q[4], and_1_out);
  not not_6 (not_6_out, and_2_out);
  not not_7 (not_7_out, and_22_out);
  Register #(.width(5)) register_1 (.D(and_24_out), .en(1'b1), .Q(register_1_q), .clk(clock_1_out));  // open: clr
  Clock clock_1 (.out(clock_1_out));
  and and_23 (and_24_out[4], or_2_out, or_1_out[6], not_6_out);
  or or_3 (or_3_out, and_3_out, and_4_out, and_5_out, and_6_out, and_7_out, and_8_out, and_9_out, and_10_out);
  or or_4 (or_4_out, and_11_out, and_12_out, and_13_out, and_14_out);
  or or_5 (or_5_out, and_15_out, and_16_out, and_17_out, and_18_out, and_19_out, and_20_out, and_21_out);
  and and_24 (and_24_out[0], not_5_out, or_1_out[6]);
  and and_25 (and_24_out[3], or_3_out, or_1_out[6], not_7_out);
  and and_26 (and_24_out[2], or_4_out, or_1_out[6], not_7_out);
  and and_27 (and_24_out[1], or_5_out, not_7_out);
  Register #(.width(7)) register_2 (
    .D({or_1_out[6], L, register_1_q}), .en(1'b1), .Q(register_2_q), .clk(clock_1_out));  // open: clr
  LED led_1 (.in(rom_1_data[3]));
  LED led_2 (.in(rom_1_data[1]));
  LED led_3 (.in(rom_1_data[0]));
  LED led_4 (.in(rom_1_data[2]));
  LED led_5 (.in(rom_1_data[7]));
  LED led_6 (.in(rom_1_data[4]));
  LED led_7 (.in(rom_1_data[6]));
  LED led_8 (.in(rom_1_data[5]));
  LED led_9 (.in(rom_1_data[8]));
  LED led_10 (.in(rom_1_data[10]));
  LED led_11 (.in(rom_1_data[9]));
  LED led_12 (.in(rom_1_data[11]));
  ROM #(.addrWidth(7), .dataWidth(20)) rom_1 (.addr(register_2_q), .data(rom_1_data));  // open: sel
  LED led_13 (.in(rom_1_data[12]));
  LED led_14 (.in(rom_1_data[15]));
  LED led_15 (.in(rom_1_data[13]));
  LED led_16 (.in(rom_1_data[14]));
  LED led_17 (.in(rom_1_data[17]));
  LED led_18 (.in(rom_1_data[16]));
  LED led_19 (.in(rom_1_data[19]));
  LED led_20 (.in(rom_1_data[18]));

  // Notes on the sheet:
  //   contents of rom_1 (hex, n*v repeats v):
  //   64*0 1 2 4 8 10 20 40 80 100 200 400 800 1000 2000 4000 8000 10000 20000 40000 80000 12*0 80000
  //   40000 20000 10000 8000 4000 2000 1000 800 400 200 100 80 40 20 10 8 4 2 1
endmodule
