// Logisim project FinalCircuit-TermProject.circ as structural Verilog: 1 circuit, main circuit main
module main (
  output [7:0] out_1,
  output [3:0] icode,
  output [3:0] ifun,
  output [7:0] out_4,
  output [3:0] rA,
  output [7:0] out_6,
  output [3:0] rB,
  output [7:0] out_8,
  output [7:0] out_9,
  output [7:0] out_10,
  output [7:0] out_11,
  output [3:0] out_12,
  output [3:0] out_13,
  output [7:0] out_14,
  output [7:0] E_Write_Data
);

  wire and_1_out, and_2_out, and_8_out, and_21_out, and_24_out, and_30_out, and_33_out, and_39_out,
       and_42_out, and_46_out, and_47_out, clock_1_out, clock_3_out, clock_4_out, clock_5_out, clock_6_out,
       clock_7_out, clock_8_out, comparator_1_eq, comparator_2_eq, comparator_2_gt, comparator_2_lt,
       decoder_1_out1, decoder_1_out2, decoder_1_out3, decoder_1_out4, decoder_1_out5, decoder_1_out6,
       decoder_1_out7, decoder_1_out8, decoder_2_out1, decoder_2_out2, decoder_2_out3, decoder_2_out4,
       decoder_2_out5, decoder_2_out6, decoder_2_out7, decoder_2_out8, multiplexer_12_out, nand_1_out,
       nand_2_out, not_2_out, or_1_out, or_2_out, or_3_out, or_4_out, or_5_out, or_6_out, or_7_out, or_8_out,
       or_13_out, or_18_out, or_23_out, or_24_out, or_27_out, register_1_q, register_9_q, register_11_q,
       register_16_q, register_17_q, register_18_q, register_19_q, register_20_q, register_21_q,
       register_22_q, s_r_ff_1_q;
  wire [1:0] multiplexer_10_out;
  wire [2:0] and_9_out;
  wire [3:0] and_4_out;
  wire [7:0] adder_1_out, adder_2_out, and_11_out, and_12_out, and_13_out, and_15_out, and_18_out,
       and_19_out, and_20_out, and_22_out, and_23_out, and_25_out, and_26_out, and_27_out, and_28_out,
       and_29_out, and_31_out, and_32_out, and_34_out, and_35_out, and_36_out, and_37_out, and_38_out,
       and_40_out, and_41_out, and_44_out, and_45_out, counter_1_q, multiplexer_1_out, multiplexer_5_out,
       multiplexer_6_out, multiplexer_7_out, multiplexer_8_out, multiplexer_13_out, multiplexer_16_out,
       multiplexer_17_out, multiplier_1_out, or_9_out, or_10_out, or_12_out, or_14_out, or_15_out, or_16_out,
       or_17_out, or_19_out, or_20_out, or_22_out, or_25_out, ram_1_data, ram_1_data_2, ram_1_data_3,
       register_3_q, register_4_q, register_5_q, register_6_q, register_8_q, register_10_q, register_12_q,
       register_13_q, register_15_q, register_23_q, register_24_q, register_26_q, subtractor_1_out,
       subtractor_2_out, xor_1_out;
  wire [7:7] and_17_out, and_43_out, clock_2_out, d_ff_1_qn, decoder_3_out1, decoder_3_out2, decoder_3_out3,
       decoder_3_out4, decoder_3_out5, decoder_3_out6, decoder_3_out7, decoder_3_out8, decoder_4_out1,
       decoder_4_out2, decoder_4_out3, decoder_4_out4, decoder_4_out5, decoder_4_out6, decoder_4_out7,
       decoder_4_out8, not_1_out, not_3_out, register_7_q, register_14_q;
  wire [15:0] register_2_q;
  wire [23:0] and_14_out, and_16_out, or_11_out, rom_1_data;
  wire [23:23] d_ff_1_q;

  Clock clock_1 (.out(clock_1_out));
  S_R_Flip_Flop s_r_ff_1 (
    .S(register_1_q), .clk(clock_1_out), .R(nand_2_out), .Q(s_r_ff_1_q));  // open: Qn, preset, reset, en
  Comparator comparator_1 (.a(8'h1), .b(register_3_q), .eq(comparator_1_eq));  // open: gt, lt
  Multiplexer #(.width(8)) multiplexer_1 (
    .in0(out_6), .in1(8'h1), .out(multiplexer_1_out), .sel(and_1_out));  // open: en
  Decoder #(.select(4)) decoder_1 (
    .out1(decoder_1_out1), .out2(decoder_1_out2), .out3(decoder_1_out3), .out4(decoder_1_out4),
    .out5(decoder_1_out5), .out6(decoder_1_out6), .out7(decoder_1_out7), .out8(decoder_1_out8), .sel(out_12));  // open: out0, out9, out10, out11, out12, out13, out14, out15, en
  Decoder #(.select(4)) decoder_2 (
    .out1(decoder_2_out1), .out2(decoder_2_out2), .out3(decoder_2_out3), .out4(decoder_2_out4),
    .out5(decoder_2_out5), .out6(decoder_2_out6), .out7(decoder_2_out7), .out8(decoder_2_out8), .sel(out_13));  // open: out0, out9, out10, out11, out12, out13, out14, out15, en
  Register #(.width(1)) register_1 (.D(comparator_1_eq), .Q(register_1_q), .clk(clock_3_out));  // open: en, clr
  Counter #(.ongoal("stay")) counter_1 (.Q(counter_1_q), .clk(clock_2_out[7]));  // open: load, D, count, carry, clr
  Clock #(.highDuration(4), .lowDuration(22)) clock_2 (.out(clock_2_out[7]));
  Register #(.width(24)) register_2 (
    .D({ram_1_data_3, ram_1_data_2, ram_1_data}), .Q({icode, ifun, register_2_q}), .clk(register_9_q));  // open: en, clr
  nand nand_1 (nand_1_out, s_r_ff_1_q, and_1_out);
  and and_1 (and_1_out, d_ff_1_qn[7], and_2_out);
  and and_2 (and_2_out, ~out_6[7], ~out_6[6], ~out_6[5], ~out_6[4], ~out_6[3], ~out_6[2], ~out_6[1], ~out_6[0]);  // AND_Gate
  Clock #(.highDuration(4), .lowDuration(22)) clock_3 (.out(clock_3_out));
  nand nand_2 (nand_2_out, counter_1_q[4], counter_1_q[7], counter_1_q[6], counter_1_q[5], counter_1_q[3], counter_1_q[2], counter_1_q[1], counter_1_q[0]);
  D_Flip_Flop d_ff_1 (
    .clk(clock_2_out[7]), .D(nand_2_out), .Q(d_ff_1_q[23]), .Qn(d_ff_1_qn[7]));  // open: preset, en, reset
  Register register_3 (.D(multiplexer_1_out), .en(d_ff_1_qn[7]), .Q(register_3_q), .clk(register_7_q[7]));  // open: clr
  Adder adder_1 (.a(register_3_q), .b(8'h1), .out(adder_1_out));  // open: cin, cout
  or or_1 (or_1_out, decoder_1_out6, decoder_2_out6);
  or or_2 (or_2_out, decoder_1_out7, decoder_2_out7);
  or or_3 (or_3_out, decoder_1_out8, decoder_2_out8);
  or or_4 (or_4_out, decoder_1_out1, decoder_2_out1);
  or or_5 (or_5_out, decoder_1_out2, decoder_2_out2);
  or or_6 (or_6_out, decoder_1_out3, decoder_2_out3);
  and and_3 (and_9_out[2], register_16_q, or_7_out);
  or or_7 (or_7_out, decoder_1_out4, decoder_2_out4);
  or or_8 (or_8_out, decoder_1_out5, decoder_2_out5);
  and and_4 (and_4_out[0], register_16_q, or_8_out);
  and and_5 (and_4_out[1], or_1_out, register_16_q);
  and and_6 (and_4_out[2], register_16_q, or_2_out);
  and and_7 (and_4_out[3], register_16_q, or_3_out);
  LED led_1 (.in(d_ff_1_qn[7]));
  Multiplexer #(.select(4), .width(4)) multiplexer_2 (
    .in0(4'b0000), .in1(4'b0000), .in2(4'b0000), .in3(register_2_q[15:12]), .in4(register_2_q[11:8]),
    .in5(register_2_q[15:12]), .in6(4'b0000), .in7(4'b0000), .in8(4'b0101), .in9(register_2_q[15:12]),
    .in10(register_2_q[15:12]), .in11(4'b0000), .in12(4'b0000), .in13(4'b0000), .in14(4'b0000),
    .in15(4'b0000), .out(rA), .sel(icode));  // open: en
  Multiplexer #(.select(4), .width(4)) multiplexer_3 (
    .in0(4'b0000), .in1(4'b0000), .in2(register_2_q[7:4]), .in3(register_2_q[11:8]),
    .in4(register_2_q[15:12]), .in5(register_2_q[11:8]), .in6(4'b0000), .in7(4'b0101), .in8(4'b0101),
    .in9(4'b0101), .in10(4'b0101), .in11(4'b0000), .in12(4'b0000), .in13(4'b0000), .in14(4'b0000),
    .in15(4'b0000), .out(rB), .sel(icode));  // open: en
  Multiplexer #(.select(4), .width(8)) multiplexer_4 (
    .in0({8{1'b0}}), .in1({8{1'b0}}), .in2(register_2_q[15:8]), .in3(register_2_q[7:0]),
    .in4(register_2_q[7:0]), .in5({8{1'b0}}), .in6(register_2_q[15:8]), .in7(register_2_q[15:8]),
    .in8({8{1'b0}}), .in9(register_2_q[15:8]), .in10(register_2_q[15:8]), .in11({8{1'b0}}), .in12({8{1'b0}}),
    .in13({8{1'b0}}), .in14({8{1'b0}}), .in15({8{1'b0}}), .out(out_11), .sel(icode));  // open: en
  and and_8 (and_8_out, or_4_out, register_16_q);
  and and_9 (and_9_out[0], or_5_out, register_16_q);
  and and_10 (and_9_out[1], or_6_out, register_16_q);
  ROM #(.dataWidth(24)) rom_1 (.addr(counter_1_q), .data(rom_1_data), .sel(d_ff_1_q[23]));
  assign and_11_out = {8{register_7_q[7]}} & register_3_q;  // AND_Gate and_11, 8 bits wide
  assign and_12_out = {8{d_ff_1_qn[7]}} & {8{register_14_q[7]}} & multiplexer_16_out;  // AND_Gate and_12, 8 bits wide
  assign and_13_out = counter_1_q & {8{d_ff_1_q[23]}};  // AND_Gate and_13, 8 bits wide
  assign and_14_out = rom_1_data & {24{d_ff_1_q[23]}};  // AND_Gate and_14, 24 bits wide
  assign or_9_out = and_11_out | and_12_out;  // OR_Gate or_9, 8 bits wide
  assign or_10_out = and_13_out | and_15_out;  // OR_Gate or_10, 8 bits wide
  assign and_15_out = or_9_out & {8{d_ff_1_qn[7]}};  // AND_Gate and_15, 8 bits wide
  assign or_11_out = and_14_out | and_16_out;  // OR_Gate or_11, 24 bits wide
  assign and_16_out = {24{d_ff_1_qn[7]}} & {{16{1'b0}}, multiplexer_13_out};  // AND_Gate and_16, 24 bits wide
  Multiplexer #(.select(4), .width(8)) multiplexer_5 (
    .in0({8{1'b0}}), .in1({8{1'b0}}), .in2(out_11), .in3(out_11), .in4(out_11), .in5(out_1), .in6({8{1'b0}}),
    .in7(8'h1), .in8(8'h1), .in9(8'h1), .in10(8'h1), .in11({8{1'b0}}), .in12({8{1'b0}}), .in13({8{1'b0}}),
    .in14({8{1'b0}}), .in15({8{1'b0}}), .out(multiplexer_5_out), .sel(icode));  // open: en
  and and_17 (and_17_out[7], icode[0], ~icode[1], icode[2], ~icode[3]);  // AND_Gate
  Clock clock_4 (.out(clock_4_out));
  assign or_12_out = and_19_out | and_18_out;  // OR_Gate or_12, 8 bits wide
  assign and_18_out = {8{decoder_4_out1[7]}} & E_Write_Data;  // AND_Gate and_18, 8 bits wide
  assign and_19_out = {8{decoder_3_out1[7]}} & out_14;  // AND_Gate and_19, 8 bits wide
  assign and_20_out = {8{decoder_3_out2[7]}} & out_14;  // AND_Gate and_20, 8 bits wide
  or or_13 (or_13_out, and_21_out, d_ff_1_q[23]);
  and and_21 (and_21_out, register_14_q[7], multiplexer_10_out[1]);
  Register register_4 (.D(or_12_out), .en(and_8_out), .Q(register_4_q), .clk(clock_4_out));  // open: clr
  assign or_14_out = and_20_out | and_23_out;  // OR_Gate or_14, 8 bits wide
  assign and_22_out = {8{decoder_3_out3[7]}} & out_14;  // AND_Gate and_22, 8 bits wide
  assign and_23_out = {8{decoder_4_out2[7]}} & E_Write_Data;  // AND_Gate and_23, 8 bits wide
  RAM #(.dataWidth(24), .bus("separate")) ram_1 (
    .addr(or_10_out), .din(or_11_out), .data({ram_1_data_3, ram_1_data_2, ram_1_data}), .str(or_13_out),
    .clk(clock_5_out), .ld(or_18_out));  // open: sel, clr
  and and_24 (and_24_out, d_ff_1_qn[7], nand_1_out, clock_2_out[7]);
  Adder adder_2 (.a(out_10), .b(multiplexer_5_out), .out(adder_2_out));  // open: cin, cout
  Subtractor subtractor_1 (.a(out_10), .b(multiplexer_5_out), .out(subtractor_1_out));  // open: bin, bout
  assign and_25_out = out_10 & multiplexer_5_out;  // AND_Gate and_25, 8 bits wide
  assign xor_1_out = out_10 ^ multiplexer_5_out;  // XOR_Gate xor_1, 8 bits wide
  assign or_15_out = out_10 | multiplexer_5_out;  // OR_Gate or_15, 8 bits wide
  Multiplier multiplier_1 (.a(out_10), .b(multiplexer_5_out), .out(multiplier_1_out));  // open: cin, cout
  Multiplexer #(.select(4), .width(8)) multiplexer_6 (
    .in0({8{1'b0}}), .in1(register_4_q), .in2(register_5_q), .in3(register_6_q), .in4(register_8_q),
    .in5(register_10_q), .in6(register_13_q), .in7(register_12_q), .in8(register_15_q),
    .out(multiplexer_6_out), .sel(rA));  // open: in9, in10, in11, in12, in13, in14, in15, en
  Register register_5 (.D(or_14_out), .en(and_9_out[0]), .Q(register_5_q), .clk(clock_4_out));  // open: clr
  Register register_6 (.D(or_16_out), .en(and_9_out[1]), .Q(register_6_q), .clk(clock_4_out));  // open: clr
  assign or_16_out = and_22_out | and_26_out;  // OR_Gate or_16, 8 bits wide
  assign or_17_out = and_27_out | and_29_out;  // OR_Gate or_17, 8 bits wide
  assign and_26_out = {8{decoder_4_out3[7]}} & E_Write_Data;  // AND_Gate and_26, 8 bits wide
  assign and_27_out = {8{decoder_3_out4[7]}} & out_14;  // AND_Gate and_27, 8 bits wide
  or or_18 (or_18_out, register_7_q[7], and_30_out);
  Register #(.width(1)) register_7 (.D(and_24_out), .Q(register_7_q[7]), .clk(clock_5_out));  // open: en, clr
  Clock #(.highDuration(2), .lowDuration(2)) clock_5 (.out(clock_5_out));
  Multiplexer #(.select(4), .width(8)) multiplexer_7 (
    .in0({8{1'b0}}), .in1({8{1'b0}}), .in2(multiplexer_5_out), .in3(adder_2_out), .in4(adder_2_out),
    .in5({8{1'b0}}), .in6({8{1'b0}}), .in7(subtractor_1_out), .in8(adder_2_out), .in9(subtractor_1_out),
    .in10(adder_2_out), .in11({8{1'b0}}), .in12({8{1'b0}}), .in13({8{1'b0}}), .in14({8{1'b0}}),
    .in15({8{1'b0}}), .out(multiplexer_7_out), .sel(icode));  // open: en
  Multiplexer #(.select(3), .width(8)) multiplexer_8 (
    .in0(adder_2_out), .in1(subtractor_1_out), .in2(and_25_out), .in3(xor_1_out), .in4(or_15_out),
    .in5(multiplier_1_out), .in6({8{1'b0}}), .in7({8{1'b0}}), .out(multiplexer_8_out), .sel(ifun[2:0]));  // open: en
  not not_1 (not_1_out[7], and_17_out[7]);
  Multiplexer #(.width(8)) multiplexer_9 (
    .in0(multiplexer_6_out), .in1(out_10), .out(out_1), .sel(and_33_out));  // open: en
  Register register_8 (.D(or_17_out), .en(and_9_out[2]), .Q(register_8_q), .clk(clock_4_out));  // open: clr
  assign or_19_out = and_28_out | and_34_out;  // OR_Gate or_19, 8 bits wide
  assign and_28_out = {8{decoder_3_out5[7]}} & out_14;  // AND_Gate and_28, 8 bits wide
  assign and_29_out = {8{decoder_4_out4[7]}} & E_Write_Data;  // AND_Gate and_29, 8 bits wide
  and and_30 (and_30_out, multiplexer_10_out[0], register_14_q[7]);
  LED led_2 (.in(register_9_q));
  LED led_3 (.in(register_7_q[7]));
  Register #(.width(1)) register_9 (.D(register_7_q[7]), .Q(register_9_q), .clk(clock_5_out));  // open: en, clr
  assign and_31_out = multiplexer_7_out & {8{not_1_out[7]}};  // AND_Gate and_31, 8 bits wide
  assign and_32_out = multiplexer_8_out & {8{and_17_out[7]}};  // AND_Gate and_32, 8 bits wide
  and and_33 (and_33_out, icode[3], ~icode[2], icode[1], ~icode[0]);  // AND_Gate
  Register register_10 (.D(or_19_out), .en(and_4_out[0]), .Q(register_10_q), .clk(clock_4_out));  // open: clr
  assign and_34_out = {8{decoder_4_out5[7]}} & E_Write_Data;  // AND_Gate and_34, 8 bits wide
  assign or_20_out = and_36_out | and_35_out;  // OR_Gate or_20, 8 bits wide
  assign and_35_out = {8{decoder_4_out6[7]}} & E_Write_Data;  // AND_Gate and_35, 8 bits wide
  assign and_36_out = {8{decoder_3_out6[7]}} & out_14;  // AND_Gate and_36, 8 bits wide
  LED led_4 (.in(register_11_q));
  Register #(.width(1)) register_11 (.D(register_9_q), .Q(register_11_q), .clk(clock_5_out));  // open: en, clr
  Comparator comparator_2 (.a({8{1'b0}}), .b(out_9), .gt(comparator_2_gt), .eq(comparator_2_eq), .lt(comparator_2_lt));
  assign out_9 = and_31_out | and_32_out;  // OR_Gate or_21, 8 bits wide
  Register register_12 (.D(or_22_out), .en(and_4_out[2]), .Q(register_12_q), .clk(clock_4_out));  // open: clr
  Register register_13 (.D(or_20_out), .en(and_4_out[1]), .Q(register_13_q), .clk(clock_4_out));  // open: clr
  assign or_22_out = and_38_out | and_37_out;  // OR_Gate or_22, 8 bits wide
  assign and_37_out = {8{decoder_4_out7[7]}} & E_Write_Data;  // AND_Gate and_37, 8 bits wide
  assign and_38_out = {8{decoder_3_out7[7]}} & out_14;  // AND_Gate and_38, 8 bits wide
  Multiplexer #(.select(4), .width(2)) multiplexer_10 (
    .in0(2'b00), .in1(2'b00), .in2(2'b00), .in3(2'b10), .in4(2'b01), .in5(2'b00), .in6(2'b00), .in7(2'b10),
    .in8(2'b01), .in9(2'b10), .in10(2'b01), .in11(2'b00), .in12(2'b00), .in13(2'b00), .in14(2'b00),
    .in15(2'b00), .out(multiplexer_10_out), .sel(icode));  // open: en
  LED led_5 (.in(register_14_q[7]));
  Register #(.width(1)) register_14 (.D(register_11_q), .Q(register_14_q[7]), .clk(clock_5_out));  // open: en, clr
  and and_39 (and_39_out, and_17_out[7], register_11_q);
  or or_23 (or_23_out, comparator_2_eq, comparator_2_gt);
  not not_2 (not_2_out, comparator_2_eq);
  or or_24 (or_24_out, comparator_2_lt, comparator_2_eq);
  Register register_15 (.D(or_25_out), .en(and_4_out[3]), .Q(register_15_q), .clk(clock_4_out));  // open: clr
  assign or_25_out = and_40_out | and_41_out;  // OR_Gate or_25, 8 bits wide
  assign and_40_out = {8{decoder_3_out8[7]}} & out_14;  // AND_Gate and_40, 8 bits wide
  assign and_41_out = {8{decoder_4_out8[7]}} & E_Write_Data;  // AND_Gate and_41, 8 bits wide
  LED led_6 (.in(register_16_q));
  Register #(.width(1)) register_16 (.D(register_14_q[7]), .Q(register_16_q), .clk(clock_5_out));  // open: en, clr
  Register #(.width(1)) register_17 (
    .D(or_23_out), .en(and_17_out[7]), .Q(register_17_q), .clk(and_39_out));  // open: clr
  Register #(.width(1)) register_18 (
    .D(comparator_2_gt), .en(and_17_out[7]), .Q(register_18_q), .clk(and_39_out));  // open: clr
  Register #(.width(1)) register_19 (
    .D(comparator_2_eq), .en(and_17_out[7]), .Q(register_19_q), .clk(and_39_out));  // open: clr
  Register #(.width(1)) register_20 (
    .D(not_2_out), .en(and_17_out[7]), .Q(register_20_q), .clk(and_39_out));  // open: clr
  Register #(.width(1)) register_21 (
    .D(or_24_out), .en(and_17_out[7]), .Q(register_21_q), .clk(and_39_out));  // open: clr
  Register #(.width(1)) register_22 (
    .D(comparator_2_lt), .en(and_17_out[7]), .Q(register_22_q), .clk(and_39_out));  // open: clr
  Clock clock_6 (.out(clock_6_out));
  Multiplexer #(.select(4), .width(8)) multiplexer_11 (
    .in0({8{1'b0}}), .in1(register_4_q), .in2(register_5_q), .in3(register_6_q), .in4(register_8_q),
    .in5(register_10_q), .in6(register_13_q), .in7(register_12_q), .in8(register_15_q), .out(out_10), .sel(rB));  // open: in9, in10, in11, in12, in13, in14, in15, en
  Multiplexer #(.select(4)) multiplexer_12 (
    .in0(1'b1), .in1(register_17_q), .in2(register_18_q), .in3(register_19_q), .in4(register_20_q),
    .in5(register_21_q), .in6(register_22_q), .in7(1'b0), .in8(1'b0), .in9(1'b0), .in10(1'b0), .in11(1'b0),
    .in12(1'b0), .in13(1'b0), .in14(1'b0), .in15(1'b0), .out(multiplexer_12_out), .sel(ifun));  // open: en
  Register register_23 (.D(out_9), .en(register_11_q), .Q(register_23_q), .clk(clock_6_out));  // open: clr
  Clock clock_7 (.out(clock_7_out));
  Multiplexer #(.select(4), .width(8)) multiplexer_13 (
    .in0({8{1'b0}}), .in1({8{1'b0}}), .in2({8{1'b0}}), .in3(out_1), .in4({8{1'b0}}), .in5({8{1'b0}}),
    .in6({8{1'b0}}), .in7(adder_1_out), .in8({8{1'b0}}), .in9(out_1), .in10({8{1'b0}}), .in11({8{1'b0}}),
    .in12({8{1'b0}}), .in13({8{1'b0}}), .in14({8{1'b0}}), .in15({8{1'b0}}), .out(multiplexer_13_out),
    .sel(icode));  // open: en
  and and_42 (and_42_out, multiplexer_10_out[0], register_14_q[7]);
  Multiplexer #(.width(8)) multiplexer_14 (
    .in0(adder_1_out), .in1(out_11), .out(out_4), .sel(multiplexer_12_out));  // open: en
  Register #(.trigger("high")) register_24 (
    .D(out_9), .en(register_9_q), .Q(register_24_q), .clk(clock_7_out));  // open: clr
  Decoder #(.select(4)) decoder_3 (
    .out1(decoder_3_out1[7]), .out2(decoder_3_out2[7]), .out3(decoder_3_out3[7]), .out4(decoder_3_out4[7]),
    .out5(decoder_3_out5[7]), .out6(decoder_3_out6[7]), .out7(decoder_3_out7[7]), .out8(decoder_3_out8[7]),
    .sel(out_12), .en(register_16_q));  // open: out0, out9, out10, out11, out12, out13, out14, out15
  Multiplexer #(.width(8)) multiplexer_15 (
    .in0(register_23_q), .in1(register_24_q), .out(E_Write_Data), .sel(or_27_out));  // open: en
  Multiplexer #(.select(4), .width(8)) multiplexer_16 (
    .in0({8{1'b0}}), .in1({8{1'b0}}), .in2({8{1'b0}}), .in3(register_23_q), .in4(register_23_q),
    .in5({8{1'b0}}), .in6({8{1'b0}}), .in7(register_23_q), .in8(out_1), .in9(subtractor_2_out),
    .in10(register_26_q), .in11({8{1'b0}}), .in12({8{1'b0}}), .in13({8{1'b0}}), .in14({8{1'b0}}),
    .in15({8{1'b0}}), .out(multiplexer_16_out), .sel(icode));  // open: en
  and and_43 (and_43_out[7], ~icode[0], icode[1], icode[2], ~icode[3]);  // AND_Gate
  assign and_44_out = {8{and_43_out[7]}} & out_4;  // AND_Gate and_44, 8 bits wide
  Multiplexer #(.select(4), .width(8)) multiplexer_17 (
    .in0({8{1'b0}}), .in1(adder_1_out), .in2(adder_1_out), .in3(adder_1_out), .in4(adder_1_out),
    .in5(adder_1_out), .in6({8{1'b0}}), .in7(out_11), .in8(out_14), .in9(adder_1_out), .in10(adder_1_out),
    .in11({8{1'b0}}), .in12({8{1'b0}}), .in13({8{1'b0}}), .in14({8{1'b0}}), .in15({8{1'b0}}),
    .out(multiplexer_17_out), .sel(icode));  // open: en
  Decoder #(.select(4)) decoder_4 (
    .out1(decoder_4_out1[7]), .out2(decoder_4_out2[7]), .out3(decoder_4_out3[7]), .out4(decoder_4_out4[7]),
    .out5(decoder_4_out5[7]), .out6(decoder_4_out6[7]), .out7(decoder_4_out7[7]), .out8(decoder_4_out8[7]),
    .sel(out_13), .en(register_16_q));  // open: out0, out9, out10, out11, out12, out13, out14, out15
  Register register_25 (.D(ram_1_data), .en(and_42_out), .Q(out_14), .clk(clock_5_out));  // open: clr
  not not_3 (not_3_out[7], and_43_out[7]);
  assign out_6 = and_44_out | and_45_out;  // OR_Gate or_26, 8 bits wide
  assign and_45_out = multiplexer_17_out & {8{not_3_out[7]}};  // AND_Gate and_45, 8 bits wide
  Multiplexer #(.select(4), .width(4)) multiplexer_18 (
    .in0(4'b0000), .in1(4'b0000), .in2(4'b0000), .in3(4'b0000), .in4(rA), .in5(4'b0000), .in6(4'b0000),
    .in7(4'b0000), .in8(4'b0000), .in9(4'b0000), .in10(rA), .in11(4'b0000), .in12(4'b0000), .in13(4'b0000),
    .in14(4'b0000), .in15(4'b0000), .out(out_12), .sel(icode));  // open: en
  Multiplexer #(.select(4), .width(4)) multiplexer_19 (
    .in0(4'b0000), .in1(4'b0000), .in2(rB), .in3(4'b0000), .in4(4'b0000), .in5(rB), .in6(4'b0000), .in7(rB),
    .in8(rB), .in9(rB), .in10(rB), .in11(4'b0000), .in12(4'b0000), .in13(4'b0000), .in14(4'b0000),
    .in15(4'b0000), .out(out_13), .sel(icode));  // open: en
  Register register_26 (.D(register_10_q), .en(register_7_q[7]), .Q(register_26_q), .clk(clock_8_out));  // open: clr
  Clock clock_8 (.out(clock_8_out));
  or or_27 (or_27_out, and_47_out, and_46_out);
  and and_46 (and_46_out, icode[0], ~icode[1], ~icode[2], icode[3]);  // AND_Gate
  Subtractor subtractor_2 (.a(register_26_q), .b(8'h1), .out(subtractor_2_out));  // open: bin, bout
  and and_47 (and_47_out, ~icode[0], icode[1], ~icode[2], icode[3]);  // AND_Gate

  assign out_8 = out_1;

  // Notes on the sheet:
  //   PC
  //   Boot
  //   PC Increment
  //   Normal Operation
  //   ROM
  //   valC
  //   Initial Boot
  //   contents of rom_1 (hex, n*v repeats v):
  //   0 20cf50 200110 20f040 301400 200210 301401 200310 301402 200410 301403 200110 20e020 301200 200010
  //   301201 200110 301202 200010 301203 200010 602200 901000 a03000 504300 403700 901000 a03000 502300
  //   403800 507800 308300 200130 503100 200430 511300 641600 705500 10*100000 37*0 200010 200470 511700
  //   645a00 607b00 200030 605c00 200270 513700 646200 200270 507100 605600 901000 a07000 903000 a08000
  //   504700 502800 407700 408800 557800 908000 200170 200280 501700 503800 504700 502800 407700 408800
  //   557800 a07000 507800 908000 200170 507300 605c00 20d010 a03000 303103 a03000 303102 a03000 303101
  //   a03000 303100 800000
  //   Initial boot
  //   Address
  //   Normal
  //   Normal
  //   Data
  //   RAM
  //   Store to mem signal
  //   rA Read
  //   0x1
  //   0x2
  //   %eax
  //   %ecx
  //   ifun
  //   0x3
  //   %edx
  //   OP
  //   valA
  //   0x4
  //   %ebx
  //   M Write Data
  //   Data to store in mem
  //   RAM Read
  //   0 > E
  //   0x6
  //   0x5
  //   %ebp
  //   %esp
  //   Read Signal
  //   IM Write
  //   0x7
  //   %esi
  //   Flags
  //   valE (ALU Output
  //   0x8
  //   %edi
  //   1 = read
  //   icode
  //   Less/Equal
  //   Less
  //   Equal
  //   Not Equal
  //   Greater/Equal
  //   Greater
  //   2 = write
  //   C
  //   Data
  //   jmpC
  //   P
  //   M
  //   valB
  //   M Write Reg Select
  //   Address
  //   jXX
  //   W Enable M
  //   W Enable E
  //   E Write Reg Select
  //   ValM
  //   !jXX
  //   icode
  //   valE
  //   valP
  //   rB
  //   rA
  //   valA
endmodule
